# Fritzing sketch Schematic (saved by Fritzing 0.9.3b)
breadboards: 1

parts:
  Part1 = 24 NeoPixel Ring [part_number=1586]
  A1 = Arduino Nano ESP32
  U1 = 74AHCT125 [part_number=SN74AHCT125 package=dil14]
  JACK1 = 2.1mm DC Barrel Jack
  M1 = RioRand LM2596

nets:
  N1: Part1.IN, U1.1Y
  VDD: Part1.VDD, U1.VCC, M1.Pin_3
  GND: Part1.GND, U1.1OE, U1.GND, M1.Pin_4
  GND_2: A1.Pin_14, JACK1.sleeve, M1.Pin_2
  N2: A1.Pin_15, JACK1.center, M1.Pin_1
  N3: A1.Pin_24, U1.1A

notes:
  5V DC
  6V-21V DC

custom parts:
  24 NeoPixel Ring: 24 ultra bright smart LED NeoPixels are arranged in a circle with 2.6" (66mm) outer diameter. The rings are 'chainable' - connect the output pin of one to the input pin of another. Use only one microcontroller pin to control as many as you can chain together! Each LED is addressable as the driver chip is inside the LED. Each one has ~18mA constant current drive so the color will be very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
  Arduino Nano ESP32: Arduino® Nano ESP32 tht.
  74AHCT125: Quad Level-Shifter (3V to 5V) Quadruple Bus Buffer Gates With 3-State Outputs
  2.1mm DC Barrel Jack: 2.1mm DC Barrel Jack with Thru-Hole Connectors (breadboardable)
